# Fritzing sketch garduino (saved by Fritzing 0.5.2b)
breadboards: 1

parts:
  4051 = mystery part, 16 pins [chip_label=? spacing=300mil]
  Arduino1 = Arduino
  LDR1 = Photocell (LDR) [package=THT]
  RLDR1 = Resistor [resistance=10k package=THT]
  RT1 = Resistor [resistance=10k package=THT]
  T1 = Temperature Sensor (Thermistor) [package=THT]
  R4 = Resistor [resistance=10k package=THT]
  R5 = Resistor [resistance=10k package=THT]
  R6 = Resistor [resistance=10k package=THT]
  R7 = Resistor [resistance=10k package=THT]
  R0 = Resistor [resistance=10k package=THT]
  R1 = Resistor [resistance=10k package=THT]
  R2 = Resistor [resistance=10k package=THT]
  R3 = Resistor [resistance=10k package=THT]
  I0 = mono mini jack
  I1 = mono mini jack
  I2 = mono mini jack
  I3 = mono mini jack
  I4 = mono mini jack
  I5 = mono mini jack
  I6 = mono mini jack
  I7 = mono mini jack

nets:
  N1: 4051.pin1, R4.Pin_0, I4.connector0
  N2: 4051.pin2, R6.Pin_0, I6.connector0
  N3: 4051.pin3, Arduino1.A0
  N4: 4051.pin4, R7.Pin_0, I7.connector0
  N5: 4051.pin5, R5.Pin_0, I5.connector0
  N6: 4051.pin6, 4051.pin7, 4051.pin8, Arduino1.GND, RLDR1.Pin_1, RT1.Pin_1, R4.Pin_1, R5.Pin_1, R6.Pin_1, R7.Pin_1, R0.Pin_0, R1.Pin_0, R2.Pin_0, R3.Pin_0
  N7: 4051.pin9, Arduino1.D2
  N8: 4051.pin10, Arduino1.D3
  N9: 4051.pin11, Arduino1.D4
  N10: 4051.pin12, R3.Pin_1, I3.connector0
  N11: 4051.pin13, R0.Pin_1, I0.connector0
  N12: 4051.pin14, R1.Pin_1, I1.connector0
  N13: 4051.pin15, R2.Pin_1, I2.connector0
  N14: 4051.pin16, Arduino1.+5V, LDR1.pin_0, T1.pin_1, I0.connector1, I1.connector1, I2.connector1, I3.connector1, I4.connector1, I5.connector1, I6.connector1, I7.connector1
  N15: Arduino1.A1, LDR1.pin_1, RLDR1.Pin_0
  N16: Arduino1.A2, RT1.Pin_0, T1.pin_0
